// Logisim project BFISA_VHDL.circ as structural Verilog: 4 circuits, main circuit main
module main (
  input  [7:0] Key
);

  wire and_1_out, and_2_out, and_3_out, and_4_out, Clk_out, dbcr_pulse, decoder_hold, decoder_jump,
       decoder_loopback, decoder_memsrc, decoder_modmem, decoder_modptr, decoder_outp, Input_Valid_out,
       nor_1_out, nor_2_out, nor_3_out, nor_4_out, not_1_out, not_2_out, not_3_out, not_4_out, not_5_out,
       or_1_out, or_2_out, Reset_out, xor_1_out;
  wire [2:0] program_data;
  wire [6:0] mem_dout;
  wire [7:0] adder_3_out, multiplexer_3_out;
  wire [7:7] decoder_memop, mem_dout_2;
  wire [15:0] adder_1_out, adder_2_out, bit_extender_1_out, multiplexer_1_out, multiplexer_2_out, PC_q,
       Pointer_q;
  wire [15:3] program_data_2;
  wire [15:15] decoder_ptrop;

  Clock Clk (.out(Clk_out));
  Button Reset (.out(Reset_out));
  Button Input_Valid (.out(Input_Valid_out));
  not not_1 (not_1_out, decoder_ptrop[15]);
  Adder #(.width(16)) adder_1 (
    .a({16{decoder_ptrop[15]}}), .b(Pointer_q), .out(adder_1_out), .cin(not_1_out));  // open: cout
  Adder #(.width(16)) adder_2 (.a(PC_q), .b({16{1'b0}}), .out(adder_2_out), .cin(1'b1));  // open: cout
  Multiplexer #(.enable("false"), .width(16)) multiplexer_1 (
    .in0(adder_2_out), .in1(bit_extender_1_out), .out(multiplexer_1_out), .sel(and_1_out));
  and and_1 (and_1_out, xor_1_out, decoder_jump);
  xor xor_1 (xor_1_out, decoder_loopback, and_3_out);
  Debouncer dbcr (.Pulse(dbcr_pulse), .Buttn(Input_Valid_out), .Clk(Clk_out), .Rst(Reset_out));
  Decode decoder (
    .Opcode(program_data), .PtrOp(decoder_ptrop[15]), .MemOp(decoder_memop[7]), .LoopBack(decoder_loopback),
    .MemSrc(decoder_memsrc), .ModPtr(decoder_modptr), .Jump(decoder_jump), .Outp(decoder_outp),
    .ModMem(decoder_modmem), .Hold(decoder_hold));
  Register #(.width(16)) Pointer (.D(adder_1_out), .en(decoder_modptr), .clk(Clk_out), .Q(Pointer_q), .clr(Reset_out));
  or or_1 (or_1_out, dbcr_pulse, not_2_out);
  not not_2 (not_2_out, decoder_hold);
  Register #(.width(16)) PC (.D(multiplexer_1_out), .en(or_1_out), .clk(Clk_out), .Q(PC_q), .clr(Reset_out));
  not not_3 (not_3_out, decoder_modptr);
  or or_2 (or_2_out, not_3_out, Clk_out);
  Multiplexer #(.enable("false"), .width(16)) multiplexer_2 (
    .in0(adder_1_out), .in1(Pointer_q), .out(multiplexer_2_out), .sel(or_2_out));
  ROM #(.addrWidth(16), .dataWidth(16)) \program  (.addr(PC_q), .data({program_data_2, program_data}));
  RAM #(.addrWidth(16)) mem (
    .addr(multiplexer_2_out), .we(decoder_modmem), .oe(1'b1), .clk(Clk_out), .din(multiplexer_3_out),
    .dout({mem_dout_2[7], mem_dout}));
  not not_4 (not_4_out, Clk_out);
  TTY #(.cols(36), .rows(21)) tty_1 (.data(mem_dout), .clk(not_4_out), .we(decoder_outp), .clr(Reset_out));
  assign bit_extender_1_out = {{3{1'b0}}, program_data_2};  // Bit_Extender bit_extender_1
  not not_5 (not_5_out, decoder_memop[7]);
  nor nor_1 (nor_1_out, mem_dout_2[7], mem_dout[6]);
  nor nor_2 (nor_2_out, mem_dout[5], mem_dout[4]);
  nor nor_3 (nor_3_out, mem_dout[3], mem_dout[2]);
  nor nor_4 (nor_4_out, mem_dout[1], mem_dout[0]);
  Adder adder_3 (
    .a({mem_dout_2[7], mem_dout}), .b({8{decoder_memop[7]}}), .out(adder_3_out), .cin(not_5_out));  // open: cout
  Multiplexer #(.enable("false"), .width(8)) multiplexer_3 (
    .in0(adder_3_out), .in1(Key), .out(multiplexer_3_out), .sel(decoder_memsrc));
  and and_2 (and_2_out, nor_1_out, nor_2_out);
  and and_3 (and_3_out, and_2_out, and_4_out);
  and and_4 (and_4_out, nor_3_out, nor_4_out);
  Hex_Digit_Display hex_digit_display_1 (.value(multiplexer_3_out[7:4]));  // open: dp
  Hex_Digit_Display hex_digit_display_2 (.value(multiplexer_3_out[3:0]));  // open: dp

  // Notes on the sheet:
  //   30 ns
  //   22 ns
  //   contents of program (hex, n*v repeats v):
  //   0 1 8*2 19c 0 4*2 124 0 2 2 0 2 2 2 0 2 2 2 0 2 4*1 3 85 0 2 0 3 0 2 0 0 2 184 1 16d 1 3 55 0 0 6 0
  //   0 3 3 3 6 7*2 6 6 2 2 2 6 0 6 1 1 3 6 0 6 2 2 2 6 6*3 6 8*3 6 0 2 6 0 2 ffff
endmodule

module Decode (
  input  [2:0] Opcode,
  output PtrOp,
  output MemOp,
  output LoopBack,
  output MemSrc,
  output ModPtr,
  output Jump,
  output Outp,
  output ModMem,
  output Hold
);

  wire and_1_out, and_2_out, nor_3_out, nor_4_out, not_1_out;

  not not_1 (not_1_out, Opcode[2]);
  nor nor_1 (ModPtr, Opcode[1], Opcode[2]);
  nor nor_2 (Jump, Opcode[1], not_1_out);
  nor nor_3 (nor_3_out, Opcode[0], not_1_out);
  and and_1 (and_1_out, Opcode[1], not_1_out);
  and and_2 (and_2_out, Opcode[0], Opcode[1]);
  and and_3 (Outp, nor_3_out, Opcode[1]);
  nor nor_4 (nor_4_out, and_1_out, and_2_out);
  not not_2 (ModMem, nor_4_out);
  and and_4 (Hold, and_2_out, Opcode[2]);

  assign LoopBack = Opcode[0];
  assign MemOp = Opcode[0];
  assign MemSrc = Opcode[2];
  assign PtrOp = Opcode[0];
endmodule

module Debouncer (
  input  Buttn,
  input  Clk,
  input  Rst,
  output Pulse
);

  wire d_ff_1_q, d_ff_2_q, d_ff_3_q, d_ff_4_q, d_ff_5_q, d_ff_6_q, d_ff_7_q, d_ff_8_q, nand_1_out,
       nand_2_out, nor_1_out;

  D_Flip_Flop d_ff_1 (.D(Buttn), .clk(Clk), .Q(d_ff_1_q), .reset(Rst));  // open: Qn, preset
  D_Flip_Flop d_ff_2 (.D(d_ff_1_q), .clk(Clk), .Q(d_ff_2_q), .reset(Rst));  // open: Qn, preset
  D_Flip_Flop d_ff_3 (.D(d_ff_2_q), .clk(Clk), .Q(d_ff_3_q), .reset(Rst));  // open: Qn, preset
  D_Flip_Flop d_ff_4 (.D(d_ff_3_q), .clk(Clk), .Q(d_ff_4_q), .reset(Rst));  // open: Qn, preset
  D_Flip_Flop d_ff_5 (.D(d_ff_4_q), .clk(Clk), .Q(d_ff_5_q), .reset(Rst));  // open: Qn, preset
  D_Flip_Flop d_ff_6 (.D(d_ff_5_q), .clk(Clk), .Q(d_ff_6_q), .reset(Rst));  // open: Qn, preset
  D_Flip_Flop d_ff_7 (.D(d_ff_6_q), .clk(Clk), .Q(d_ff_7_q), .reset(Rst));  // open: Qn, preset
  D_Flip_Flop d_ff_8 (.D(d_ff_7_q), .clk(Clk), .Q(d_ff_8_q), .reset(Rst));  // open: Qn, preset
  nor nor_1 (nor_1_out, d_ff_8_q, d_ff_8_q);
  nand nand_1 (nand_1_out, d_ff_7_q, d_ff_6_q, d_ff_5_q, d_ff_4_q);
  nand nand_2 (nand_2_out, d_ff_3_q, d_ff_2_q, d_ff_1_q, nor_1_out);
  nor nor_2 (Pulse, nand_1_out, nand_2_out);
endmodule

module main_synth (
  input  Clk,
  input  Rst,
  input  Input_valid,
  input  [7:0] Key,
  output [6:0] Char_out,
  output out_enable
);

  wire and_1_out, and_2_out, and_3_out, and_4_out, dbcr_pulse, decoder_hold, decoder_jump, decoder_loopback,
       decoder_memsrc, decoder_modmem, decoder_modptr, nor_1_out, nor_2_out, nor_3_out, nor_4_out, not_1_out,
       not_2_out, not_3_out, not_4_out, or_1_out, or_2_out, xor_1_out;
  wire [2:0] program_data;
  wire [7:0] adder_3_out, multiplexer_3_out;
  wire [7:7] decoder_memop, mem_dout;
  wire [15:0] adder_1_out, adder_2_out, bit_extender_1_out, multiplexer_1_out, multiplexer_2_out, PC_q,
       Pointer_q;
  wire [15:3] program_data_2;
  wire [15:15] decoder_ptrop;

  not not_1 (not_1_out, decoder_ptrop[15]);
  Adder #(.width(16)) adder_1 (
    .a({16{decoder_ptrop[15]}}), .b(Pointer_q), .out(adder_1_out), .cin(not_1_out));  // open: cout
  Adder #(.width(16)) adder_2 (.a(PC_q), .b({16{1'b0}}), .out(adder_2_out), .cin(1'b1));  // open: cout
  Multiplexer #(.enable("false"), .width(16)) multiplexer_1 (
    .in0(adder_2_out), .in1(bit_extender_1_out), .out(multiplexer_1_out), .sel(and_1_out));
  and and_1 (and_1_out, xor_1_out, decoder_jump);
  xor xor_1 (xor_1_out, decoder_loopback, and_3_out);
  Debouncer dbcr (.Pulse(dbcr_pulse), .Buttn(Input_valid), .Clk(Clk), .Rst(Rst));
  Decode decoder (
    .Opcode(program_data), .PtrOp(decoder_ptrop[15]), .MemOp(decoder_memop[7]), .LoopBack(decoder_loopback),
    .MemSrc(decoder_memsrc), .ModPtr(decoder_modptr), .Jump(decoder_jump), .Outp(out_enable),
    .ModMem(decoder_modmem), .Hold(decoder_hold));
  Register #(.width(16)) Pointer (.D(adder_1_out), .en(decoder_modptr), .clk(Clk), .Q(Pointer_q), .clr(Rst));
  or or_1 (or_1_out, dbcr_pulse, not_2_out);
  not not_2 (not_2_out, decoder_hold);
  Register #(.width(16)) PC (.D(multiplexer_1_out), .en(or_1_out), .clk(Clk), .Q(PC_q), .clr(Rst));
  not not_3 (not_3_out, decoder_modptr);
  or or_2 (or_2_out, not_3_out, Clk);
  Multiplexer #(.enable("false"), .width(16)) multiplexer_2 (
    .in0(adder_1_out), .in1(Pointer_q), .out(multiplexer_2_out), .sel(or_2_out));
  ROM #(.addrWidth(16), .dataWidth(16)) \program  (.addr(PC_q), .data({program_data_2, program_data}));
  RAM #(.addrWidth(16)) mem (
    .addr(multiplexer_2_out), .we(decoder_modmem), .oe(1'b1), .clk(Clk), .din(multiplexer_3_out),
    .dout({mem_dout[7], Char_out}));
  assign bit_extender_1_out = {{3{1'b0}}, program_data_2};  // Bit_Extender bit_extender_1
  not not_4 (not_4_out, decoder_memop[7]);
  nor nor_1 (nor_1_out, mem_dout[7], Char_out[6]);
  nor nor_2 (nor_2_out, Char_out[5], Char_out[4]);
  nor nor_3 (nor_3_out, Char_out[3], Char_out[2]);
  nor nor_4 (nor_4_out, Char_out[1], Char_out[0]);
  Adder adder_3 (
    .a({mem_dout[7], Char_out}), .b({8{decoder_memop[7]}}), .out(adder_3_out), .cin(not_4_out));  // open: cout
  Multiplexer #(.enable("false"), .width(8)) multiplexer_3 (
    .in0(adder_3_out), .in1(Key), .out(multiplexer_3_out), .sel(decoder_memsrc));
  and and_2 (and_2_out, nor_1_out, nor_2_out);
  and and_3 (and_3_out, and_2_out, and_4_out);
  and and_4 (and_4_out, nor_3_out, nor_4_out);

  // Notes on the sheet:
  //   contents of program (hex, n*v repeats v):
  //   0 1 8*2 19c 0 4*2 124 0 2 2 0 2 2 2 0 2 2 2 0 2 4*1 3 85 0 2 0 3 0 2 0 0 2 184 1 16d 1 3 55 0 0 6 0
  //   0 3 3 3 6 7*2 6 6 2 2 2 6 0 6 1 1 3 6 0 6 2 2 2 6 6*3 6 8*3 6 0 2 6 0 2 ffff
endmodule
